// Logisim project DMX circuit 2.circ as structural Verilog: 1 circuit, main circuit main
module main (
  input  in_1,
  input  [1:0] in_2
);

  wire demultiplexer_1_out0, demultiplexer_1_out1, demultiplexer_1_out2, demultiplexer_1_out3;

  Demultiplexer #(.select(2)) demultiplexer_1 (
    .out0(demultiplexer_1_out0), .out1(demultiplexer_1_out1), .out2(demultiplexer_1_out2),
    .out3(demultiplexer_1_out3), .in(in_1), .sel(in_2));  // open: en
  LED I0 (.in(demultiplexer_1_out0));
  LED I1 (.in(demultiplexer_1_out1));
  LED I2 (.in(demultiplexer_1_out2));
  LED I3 (.in(demultiplexer_1_out3));
endmodule
