// Logisim project Pri circuit 1.circ as structural Verilog: 1 circuit, main circuit main
module main (
  input  in_1,
  input  [1:0] in_2,
  input  in_3,
  input  in_4,
  input  in_5,
  input  ENABLE,
  output out_7
);

  Priority_Encoder #(.select(2)) priority_encoder_1 (
    .in0(in_1), .in1(in_3), .in2(in_4), .in3(in_5), .out(in_2), .gs(out_7), .en_in(ENABLE));  // open: en_out
endmodule
