// Logisim project Pri circuit 2.circ as structural Verilog: 1 circuit, main circuit main
module main (
  input  _0,
  input  _1,
  input  _2,
  input  [2:0] Binary,
  input  _3,
  input  _4,
  input  _5,
  input  _6,
  input  in_9,
  input  _7
);

  Priority_Encoder priority_encoder_1 (
    .in0(_0), .in1(_1), .in2(_2), .in3(_3), .in4(_4), .in5(_5), .in6(_6), .in7(_7), .out(Binary), .en_in(in_9));  // open: gs, en_out
endmodule
