// Logisim project Project 2 circuit.circ as structural Verilog: 1 circuit, main circuit main
module main (
  input  A,
  input  B,
  output Z
);

  wire AND_2_out, AND_out, NOT_2_out, NOT_out;

  not NOT (NOT_out, A);
  not NOT_2 (NOT_2_out, B);
  and AND (AND_out, B, NOT_out);
  and AND_2 (AND_2_out, NOT_2_out, A);
  or OR (Z, AND_out, AND_2_out);
endmodule
