// Logisim project Project 4circuit.circ as structural Verilog: 1 circuit, main circuit main
module main (
  input  A,
  input  B,
  input  C,
  output Z
);

  wire AND_2_out, AND_out, NOT_2_out, NOT_out, OR_out;

  and AND (AND_out, A, B, C);
  not NOT (NOT_out, B);
  not NOT_2 (NOT_2_out, C);
  or OR (OR_out, NOT_out, NOT_2_out);
  and AND_2 (AND_2_out, A, OR_out);
  or OR_2 (Z, AND_out, AND_2_out);
endmodule
