// Logisim project Project 5 circuit.circ as structural Verilog: 1 circuit, main circuit main
module main (
  input  A,
  input  B,
  input  C,
  input  D,
  output Z
);

  wire AND_out, NOR_out, NOT_2_out, NOT_out, OR_out, XOR_out;

  not NOT (NOT_out, D);
  xor NOR (NOR_out, A, D);
  and AND (AND_out, A, NOT_out);
  or OR (OR_out, C, NOR_out);
  xor XOR (XOR_out, AND_out, B);
  not NOT_2 (NOT_2_out, OR_out);
  or OR_2 (Z, XOR_out, NOT_2_out);
endmodule
