// Logisim project Project 9 circuit.circ as structural Verilog: 1 circuit, main circuit main
module main (
  input  A,
  input  B,
  input  C,
  output X
);

  wire AND_2_out, AND_3_out, AND_out, NOT_out, OR_out;

  and AND (AND_out, A, B);
  or OR (OR_out, A, B);
  not NOT (NOT_out, C);
  and AND_2 (AND_2_out, AND_out, C);
  and AND_3 (AND_3_out, NOT_out, OR_out);
  or OR_2 (X, AND_2_out, AND_3_out);
endmodule
