// Logisim project Project Circuit 3.circ as structural Verilog: 1 circuit, main circuit main
module main (
  input  A,
  input  B,
  input  C,
  output Y
);

  wire NAND_out, NOT_out;

  nand NAND (NAND_out, A, B);
  not NOT (NOT_out, C);
  and AND (Y, NAND_out, B, NOT_out);
endmodule
