// Logisim project Project circuit 7.circ as structural Verilog: 1 circuit, main circuit main
module main (
  input  A,
  input  B,
  input  C,
  output X
);

  wire NAND_2_out, NAND_out, NOT_out;

  not NOT (NOT_out, A);
  nand NAND (NAND_out, A, B);
  nand NAND_2 (NAND_2_out, NOT_out, C);
  nand NAND_3 (X, NAND_out, NAND_2_out);
endmodule
